# Fritzing sketch esquematico_sensor_com_mcp3008 (saved by Fritzing 0.9.4)
breadboards: 1

parts:
  IC1 = MCP3008 8-channel 10-bit ADC [part_number=MCP3008]
  MQ-135 = Gas Sensor Breakout Board
  R4 = Resistor [tolerance=±5% resistance=10k package="0805 [SMD]"]
  R5 = Resistor [tolerance=±5% resistance=10k package="0805 [SMD]"]
  R6 = Resistor [tolerance=±5% resistance=10k package="0805 [SMD]"]
  R8 = Resistor [tolerance=±5% resistance=750k package="0805 [SMD]"]
  U10 = Hirose DF13 Series Header [part_number=DF13#-8P-1.25V package=DF13C-8P-1.25V]
  MQ-131 = Gas Sensor Breakout Board
  R9 = Resistor [tolerance=±5% resistance=360k package="0805 [SMD]"]
  M1 = BME280
  MCU1 = Raspberry Pi Zero

nets:
  N1: IC1.no_name_yet#1, R4.Pin_1, R5.Pin_0
  N2: IC1.no_name_yet#2, R8.Pin_0, R9.Pin_1
  GND: IC1.no_name_yet#9, IC1.no_name_yet#14, MQ-135.GND, R6.Pin_1, R8.Pin_1, U10.7, MQ-131.GND, M1.GND, MCU1.pin_6, MCU1.pin_14, MCU1.pin_34, MCU1.pin_39
  N3: IC1.no_name_yet#10, MCU1.pin_29
  N4: IC1.no_name_yet#11, MCU1.pin_19
  N5: IC1.no_name_yet#12, MCU1.pin_21
  N6: IC1.no_name_yet#13, MCU1.pin_23
  N7: IC1.no_name_yet#15, IC1.no_name_yet#16, M1.VIN, MCU1.pin_17
  N8: MQ-135.AOUT, MQ-135.DOUT, R4.Pin_0
  5V: MQ-135.5V, U10.8, MQ-131.DOUT, MQ-131.5V, MCU1.pin_2, MCU1.pin_4
  N9: R5.Pin_1, R6.Pin_0
  N10: U10.4, MCU1.pin_10
  N11: U10.5, MCU1.pin_8
  N12: MQ-131.AOUT, R9.Pin_0
  N13: M1.SCL, MCU1.pin_5
  N14: M1.SDA, MCU1.pin_3

custom parts:
  Gas Sensor Breakout Board: Gas sensor breakout board. Input voltage is 5V. Sensor output is available in analog and digital.
  BME280: Temperature Humidity Barometric presure Sensor
